# Fritzing sketch schematic (saved by Fritzing 0.9.10)

parts:
  4S_LiPo_Battery = 4S LiPo Battery
  Main_Switch = Main Power Switch
  Main_Fuse = Main DC Fuse
  Power_Distribution = Positive Power Distribution
  12_V_Motor_Supply_Regulator = Motor Supply Regulator
  Pi_5_V_DC-DC_(5_A_target) = Raspberry Pi DC-DC Regulator
  MP1584EN_LiDAR_5_V_Buck = MP1584EN LiDAR Buck Converter
  Raspberry_Pi_5 = Raspberry Pi 5
  L298N_-_LEFT = L298N Motor Driver Module
  L298N_-_RIGHT = L298N Motor Driver Module
  LEFT_12_V_ENCODER_MOTOR = 12V DC Motor with Encoder
  RIGHT_12_V_ENCODER_MOTOR = 12V DC Motor with Encoder
  RPLIDAR_S3_/_USB_Adapter = RPLIDAR S3 USB Adapter
  Common_Ground_Markers = Common Ground Markers (internally connected)

nets:
  N1: 4S_LiPo_Battery.BAT+, Main_Switch.IN, Main_Switch.OUT, Main_Fuse.IN, Main_Fuse.OUT, Power_Distribution.+IN, Power_Distribution.+MOTOR, Power_Distribution.+PI, Power_Distribution.+LIDAR, 12_V_Motor_Supply_Regulator.VIN+, Pi_5_V_DC-DC_(5_A_target).VIN+, MP1584EN_LiDAR_5_V_Buck.VIN+
  GND: 4S_LiPo_Battery.BAT-, 12_V_Motor_Supply_Regulator.GND, Pi_5_V_DC-DC_(5_A_target).GND, MP1584EN_LiDAR_5_V_Buck.GND, Raspberry_Pi_5.GND, L298N_-_LEFT.GND, L298N_-_RIGHT.GND, LEFT_12_V_ENCODER_MOTOR.ENC_GND, RIGHT_12_V_ENCODER_MOTOR.ENC_GND, RPLIDAR_S3_/_USB_Adapter.GND, Common_Ground_Markers.GND1, Common_Ground_Markers.GND2, Common_Ground_Markers.GND3, Common_Ground_Markers.GND4, Common_Ground_Markers.GND5, Common_Ground_Markers.GND6, Common_Ground_Markers.GND7, Common_Ground_Markers.GND8, Common_Ground_Markers.GND9, Common_Ground_Markers.GND10
  N2: 12_V_Motor_Supply_Regulator.VOUT+, L298N_-_LEFT.VS, L298N_-_RIGHT.VS
  N3: Pi_5_V_DC-DC_(5_A_target).VOUT+, Raspberry_Pi_5.5V
  N4: MP1584EN_LiDAR_5_V_Buck.VOUT+, RPLIDAR_S3_/_USB_Adapter.+5V_EXT
  N5: Raspberry_Pi_5.USB_D-, RPLIDAR_S3_/_USB_Adapter.USB_D+
  N6: Raspberry_Pi_5.USB_VBUS, RPLIDAR_S3_/_USB_Adapter.USB_D-
  N7: Raspberry_Pi_5.GPIO12, L298N_-_LEFT.ENA
  N8: Raspberry_Pi_5.GPIO5, L298N_-_LEFT.IN1
  N9: Raspberry_Pi_5.GPIO6, L298N_-_LEFT.IN2
  N10: Raspberry_Pi_5.GPIO13, L298N_-_RIGHT.ENA
  N11: Raspberry_Pi_5.GPIO16, L298N_-_RIGHT.IN1
  N12: Raspberry_Pi_5.GPIO20, L298N_-_RIGHT.IN2
  N13: Raspberry_Pi_5.GPIO17, LEFT_12_V_ENCODER_MOTOR.ENC_A
  N14: Raspberry_Pi_5.GPIO27, LEFT_12_V_ENCODER_MOTOR.ENC_B
  N15: Raspberry_Pi_5.GPIO22, RIGHT_12_V_ENCODER_MOTOR.ENC_A
  N16: Raspberry_Pi_5.GPIO23, RIGHT_12_V_ENCODER_MOTOR.ENC_B
  N17: Raspberry_Pi_5.3V3, LEFT_12_V_ENCODER_MOTOR.ENC_VCC, RIGHT_12_V_ENCODER_MOTOR.ENC_VCC
  N18: L298N_-_LEFT.OUT1, LEFT_12_V_ENCODER_MOTOR.M+
  N19: L298N_-_LEFT.OUT2, LEFT_12_V_ENCODER_MOTOR.M-
  N20: L298N_-_RIGHT.OUT1, RIGHT_12_V_ENCODER_MOTOR.M+
  N21: L298N_-_RIGHT.OUT2, RIGHT_12_V_ENCODER_MOTOR.M-

custom parts:
  4S LiPo Battery: Custom schematic symbol for the Otonom Arac wiring sketch.
  Main Power Switch: Custom schematic symbol for the Otonom Arac wiring sketch.
  Main DC Fuse: Custom schematic symbol for the Otonom Arac wiring sketch.
  Positive Power Distribution: Custom schematic symbol for the Otonom Arac wiring sketch.
  Motor Supply Regulator: Custom schematic symbol for the Otonom Arac wiring sketch.
  Raspberry Pi DC-DC Regulator: Custom schematic symbol for the Otonom Arac wiring sketch.
  MP1584EN LiDAR Buck Converter: Custom schematic symbol for the Otonom Arac wiring sketch.
  Raspberry Pi 5: Custom schematic symbol for the Otonom Arac wiring sketch.
  L298N Motor Driver Module: Custom schematic symbol for the Otonom Arac wiring sketch.
  12V DC Motor with Encoder: Custom schematic symbol for the Otonom Arac wiring sketch.
  RPLIDAR S3 USB Adapter: Custom schematic symbol for the Otonom Arac wiring sketch.
  Common Ground Markers (internally connected): Custom schematic symbol for the Otonom Arac wiring sketch.

// code stored in the sketch: README.txt
OTONOM ARAC - Fritzing wiring sketch

Open schematic.fzz in Fritzing and select Schematic view.
The custom part symbols are conceptual editable blocks, not manufacturer CAD footprints.

Architecture shown:
- 4S LiPo -> main switch -> fuse -> positive distribution block.
- Separate regulated motor supply for the 12 V motors (do not connect 4S directly to them).
- Separate Pi DC-DC supply (5 V / 5 A target).
- Separate MP1584EN buck converter for RPLIDAR S3 power.
- RPLIDAR USB data D+/D- only; VBUS is intentionally left unconnected in this diagram to avoid power backfeed.
- Both motors have separate motor and encoder connections.
- Ground terminals join a common ground bus.

The L298N 5V-EN jumper depends on the specific module; the schematic does not assume an external logic 5 V wire.
This file is generated as a symbolic schematic. Open it in Fritzing to inspect or adjust the drawing.
